// Logisim project cmos-and.circ as structural Verilog: 1 circuit, main circuit main
module main (
  input  A,
  input  B,
  output Y
);

  wire transistor_1_out, transistor_3_out;

  Transistor #(.\type ("p"), .gate("tl")) transistor_1 (.in(1'b1), .out(transistor_1_out), .gate(A));
  Transistor #(.\type ("n"), .gate("tl")) transistor_2 (.in(transistor_3_out), .out(transistor_1_out), .gate(A));
  Transistor #(.\type ("n"), .gate("tl")) transistor_3 (.in(1'b0), .out(transistor_3_out), .gate(B));
  Transistor #(.\type ("p"), .gate("br")) transistor_4 (.in(1'b1), .out(transistor_1_out), .gate(B));
  Transistor #(.\type ("p"), .gate("tl")) transistor_5 (.in(1'b1), .out(Y), .gate(transistor_1_out));
  Transistor #(.\type ("n"), .gate("tl")) transistor_6 (.in(1'b0), .out(Y), .gate(transistor_1_out));
endmodule
