// Logisim project cmos-nand.circ as structural Verilog: 1 circuit, main circuit main
module main (
  input  A,
  input  B,
  output Y
);

  wire transistor_4_out;

  Transistor #(.\type ("p"), .gate("tl")) transistor_1 (.in(1'b1), .out(Y), .gate(A));
  Transistor #(.\type ("p"), .gate("br")) transistor_2 (.in(1'b1), .out(Y), .gate(B));
  Transistor #(.\type ("n"), .gate("tl")) transistor_3 (.in(transistor_4_out), .out(Y), .gate(A));
  Transistor #(.\type ("n"), .gate("tl")) transistor_4 (.in(1'b0), .out(transistor_4_out), .gate(B));
endmodule
